# Fritzing sketch Untitled Sketch (saved by Fritzing 0.9.4)
breadboards: 1

parts:
  Компонент1 = Arduino Nano (Rev3.0) (ICSP)
  Raspberry_Pi_2 = Raspberry Pi 3 [part_number=RPI-3-V1.2]  # not connected
  M1 = Dagu DGServo 9g (Top view) [part_number=RS001B]  # not connected
  M2 = Dagu DGServo 9g (Top view) [part_number=RS001B]  # not connected
  M3 = BMP280  # not connected
  RGB_LED1 = RGB LED
  Mod1 = MQ-7 breakout
  module1 = Rain Detection board  # not connected
  U1 = ADMP504 - Ultralow Noise Microphone with Bottom Port and Analog Output [part_number=ADMP504]  # not connected
  U2 = AD22151 - Linear Output Magnetic Field Sensor [part_number=AD22151]  # not connected
  U3 = ADP3300 - High Accuracy 50mA Low Dropout Linear Regulator [part_number=ADP3300]  # not connected
  RGB_LED2 = RGB LED  # not connected
  RGB_LED3 = RGB LED  # not connected
  RGB_LED4 = RGB LED  # not connected
  RGB_LED5 = RGB LED  # not connected
  U4 = ADMP504 - Ultralow Noise Microphone with Bottom Port and Analog Output [part_number=ADMP504]
  U5 = ADP3300 - High Accuracy 50mA Low Dropout Linear Regulator [part_number=ADP3300]

nets:
  N1: Компонент1.D11/MOSI, RGB_LED1.pin2
  N2: Компонент1.A5, Mod1.AO, U5.NC
  N3: RGB_LED1.pin1, U4.GND
  N4: RGB_LED1.pin3, U4.OUTPUT
  N5: U4.VDD, U4.NC

notes:
  Питание

custom parts:
  BMP280: Temperature Humidity Barometric presure Sensor, I2C
  MQ-7 breakout: MQ-5 gas sensor
  Rain Detection board: Rain Detection board for ZHIYU Sensor Kit (along with LM393).
