# Fritzing sketch Untitled Sketch2 (saved by Fritzing 0.9.4)
breadboards: 1

parts:
  Компонент1 = Arduino Nano (Rev3.0) (ICSP)
  Raspberry_Pi_2 = Raspberry Pi 3 [part_number=RPI-3-V1.2]  # not connected
  M1 = Dagu DGServo 9g (Top view) [part_number=RS001B]
  M2 = Dagu DGServo 9g (Top view) [part_number=RS001B]
  RGB_LED1 = RGB LED
  Mod1 = MQ-7 breakout
  RGB_LED2 = RGB LED  # not connected
  RGB_LED3 = RGB LED  # not connected
  RGB_LED4 = RGB LED  # not connected
  RGB_LED5 = RGB LED  # not connected
  U4 = ADMP504 - Ultralow Noise Microphone with Bottom Port and Analog Output [part_number=ADMP504]
  U7 = Unproven [package=drc-10]
  U8 = ADMP504 - Ultralow Noise Microphone with Bottom Port and Analog Output [part_number=ADMP504]
  U9 = ADMP504 - Ultralow Noise Microphone with Bottom Port and Analog Output [part_number=ADMP504]
  U10 = Unproven [package=drc-10]
  U11 = Graphical LCD 128x64 [package=1x20]  # not connected
  U12 = Graphical LCD 128x64 [package=1x20]  # not connected
  U13 = Graphical LCD 128x64 [package=1x20]  # not connected
  U14 = Graphical LCD 128x64 [package=1x20]  # not connected
  M3 = BMP280
  Mod2 = YL-83 Rain Sensor - Detection Board
  Mod3 = YL-83 Rain Sensor - Control Board

nets:
  GND: Компонент1.GND, M1.gnd, M2.gnd, RGB_LED1.pin1, Mod1.GND, U4.GND, U7.ISET2, U10.ISET2, M3.SCL, Mod3.GND
  N1: Компонент1.D3, U7.ETP
  N2: Компонент1.D4, U7.OUT
  N3: Компонент1.D5, U7.~CE
  N4: Компонент1.D6, U10.ETP
  N5: Компонент1.D7, U10.OUT
  N6: Компонент1.D8, U10.~CE
  N7: Компонент1.D9, M2.pulse
  N8: Компонент1.D10, M1.pulse
  N9: Компонент1.D11/MOSI, RGB_LED1.pin2
  5V: Компонент1.5V, Mod1.AO, U7.~PG, U10.~PG, Mod3.VCC
  N10: Компонент1.A5, M3.GND
  N11: Компонент1.A4, M3.VIN
  N12: Компонент1.A1, Mod3.AO
  N13: Компонент1.A0, Mod1.DO
  N14: Компонент1.3V3, M3.SDA
  VCC: M1.vcc, M2.vcc, RGB_LED1.pin3, U4.OUTPUT
  N15: U4.VDD, U4.NC
  N16: U7.USB, U7.STAT1, U8.VDD
  N17: U7.STAT2, U8.NC
  N18: U9.VDD, U10.STAT1
  N19: U9.NC, U10.STAT2
  N20: Mod2.POS, Mod3.POS
  N21: Mod2.NEG, Mod3.NEG

custom parts:
  MQ-7 breakout: MQ-5 gas sensor
  BMP280: Temperature Humidity Barometric presure Sensor, I2C
  YL-83 Rain Sensor - Detection Board: The YL-83 is a rain sensor that has more resistance when dry and less resistance when wet. The module runs at 5V.
  YL-83 Rain Sensor - Control Board: The YL-83 is a rain sensor that has more resistance when dry and less resistance when wet. The module runs at 5V.
